// Logisim project cpu.circ as structural Verilog: 5 circuits, main circuit main
module main (
);

  wire Add, AddI, And, and_1_out, Beq, clock_1_out, Jump, Load, Mult, not_1_out, not_2_out, not_3_out,
       not_4_out, Or, Reset_out, Store, Sub, Tipo_R;
  wire [1:0] controlled_buffer_4_out_5;
  wire [3:0] bit_extender_1_out, bit_extender_2_out, bit_extender_3_out, bit_extender_4_out,
       controlled_buffer_3_out, controlled_buffer_4_out_2, controlled_buffer_4_out_3,
       controlled_buffer_4_out_4, controlled_buffer_5_out, controlled_buffer_5_out_2,
       controlled_buffer_5_out_3, controlled_buffer_5_out_4;
  wire [4:0] controlled_buffer_1_out, controlled_buffer_2_out, Rd, Rs, Rt;
  wire [4:4] controlled_buffer_3_out_2;
  wire [11:0] controlled_buffer_4_out;
  wire [15:0] Address;
  wire [25:0] JAddress, JAdress;
  wire [27:0] Data;
  wire [31:0] pc_1_data;

  pc pc_1 (.clk(clock_1_out), .reset(Reset_out), .data(pc_1_data));
  Clock clock_1 (.out(clock_1_out));
  Button Reset (.out(Reset_out));
  _7_Segment_Display u_7_segment_display_1 (
    .g(Data[17]), .f(Data[16]), .a(Data[15]), .b(Data[14]), .e(Data[18]), .d(Data[19]), .c(Data[20]));  // open: dp
  _7_Segment_Display u_7_segment_display_2 (
    .g(Data[24]), .f(Data[23]), .a(Data[22]), .b(Data[21]), .e(Data[25]), .d(Data[26]), .c(Data[27]));  // open: dp
  decoder decoder_1 (
    .Address(pc_1_data), .Tipo_R(Tipo_R), .Address_2(Address), .Rd(Rd), .Rt(Rt), .Rs(Rs), .JAddress(JAdress),
    .Add(Add), .Sub(Sub), .And(And), .Or(Or), .Mult(Mult), .Beq(Beq), .AddI(AddI), .Load(Load),
    .Store(Store), .Jump(Jump));
  Multiplexer #(.width(28), .disabled(0), .enable("false")) multiplexer_1 (
    .in1(28'hbfe7c80), .out(Data), .sel(Add));  // open: in0
  Multiplexer #(.width(28), .disabled(0), .enable("false")) multiplexer_2 (
    .in1(28'hf9d7700), .out(Data), .sel(Sub));  // open: in0
  Multiplexer #(.width(28), .disabled(0), .enable("false")) multiplexer_3 (
    .in1(28'hbf5fc80), .out(Data), .sel(And));  // open: in0
  Multiplexer #(.width(28), .disabled(0), .enable("false")) multiplexer_4 (
    .in1(28'hee58000), .out(Data), .sel(Or));  // open: in0
  Multiplexer #(.width(28), .disabled(0), .enable("false")) multiplexer_5 (
    .in1(28'hb5d5a3c), .out(Data), .sel(Mult));  // open: in0
  Multiplexer #(.width(28), .disabled(0), .enable("false")) multiplexer_6 (
    .in1(28'hf8fe780), .out(Data), .sel(Beq));  // open: in0
  _7_Segment_Display u_7_segment_display_3 (
    .g(Data[10]), .f(Data[9]), .a(Data[8]), .b(Data[7]), .e(Data[11]), .d(Data[12]), .c(Data[13]));  // open: dp
  _7_Segment_Display u_7_segment_display_4 (
    .g(Data[3]), .f(Data[2]), .a(Data[1]), .b(Data[0]), .e(Data[4]), .d(Data[5]), .c(Data[6]));  // open: dp
  Multiplexer #(.width(28), .disabled(0), .enable("false")) multiplexer_7 (
    .in1(28'hbfe7c94), .out(Data), .sel(AddI));  // open: in0
  Multiplexer #(.width(28), .disabled(0), .enable("false")) multiplexer_8 (
    .in1(28'h69deff9), .out(Data), .sel(Load));  // open: in0
  Multiplexer #(.width(28), .disabled(0), .enable("false")) multiplexer_9 (
    .in1(28'hdcf0000), .out(Data), .sel(Store));  // open: in0
  Multiplexer #(.width(28), .disabled(0), .enable("false")) multiplexer_10 (
    .in1(28'hc3d6d1f), .out(Data), .sel(Jump));  // open: in0
  Hex_Digit_Display hex_digit_display_1 (.value(bit_extender_2_out));  // open: dp
  assign controlled_buffer_1_out = not_1_out ? Rs : 5'bz;  // Controlled_Buffer controlled_buffer_1
  Hex_Digit_Display hex_digit_display_2 (.value(bit_extender_1_out));  // open: dp
  assign bit_extender_1_out = {{2{1'b0}}, controlled_buffer_4_out_5};  // Bit_Extender bit_extender_1
  Hex_Digit_Display hex_digit_display_3 (.value(controlled_buffer_1_out[3:0]));  // open: dp
  assign bit_extender_2_out = {{3{1'b0}}, controlled_buffer_1_out[4]};  // Bit_Extender bit_extender_2
  assign controlled_buffer_2_out = not_2_out ? Rt : 5'bz;  // Controlled_Buffer controlled_buffer_2
  not not_1 (not_1_out, Jump);
  Hex_Digit_Display hex_digit_display_4 (.value(controlled_buffer_4_out_4));  // open: dp
  Hex_Digit_Display hex_digit_display_5 (.value(bit_extender_3_out));  // open: dp
  assign bit_extender_3_out = {{3{1'b0}}, controlled_buffer_2_out[4]};  // Bit_Extender bit_extender_3
  not not_2 (not_2_out, Jump);
  Hex_Digit_Display hex_digit_display_6 (.value(controlled_buffer_4_out_3));  // open: dp
  Hex_Digit_Display hex_digit_display_7 (.value(bit_extender_4_out));  // open: dp
  Hex_Digit_Display hex_digit_display_8 (.value(controlled_buffer_2_out[3:0]));  // open: dp
  assign {controlled_buffer_3_out_2[4], controlled_buffer_3_out} = Tipo_R ? Rd : 5'bz;  // Controlled_Buffer controlled_buffer_3
  Hex_Digit_Display hex_digit_display_9 (.value(controlled_buffer_4_out[11:8]));  // open: dp
  Hex_Digit_Display hex_digit_display_10 (.value(controlled_buffer_4_out_2));  // open: dp
  assign {controlled_buffer_4_out_5, controlled_buffer_4_out_4, controlled_buffer_4_out_3, controlled_buffer_4_out_2, controlled_buffer_4_out} = Jump ? JAddress : 26'bz;  // Controlled_Buffer controlled_buffer_4
  Hex_Digit_Display hex_digit_display_11 (.value(controlled_buffer_3_out));  // open: dp
  assign bit_extender_4_out = {{3{1'b0}}, controlled_buffer_3_out_2[4]};  // Bit_Extender bit_extender_4
  Hex_Digit_Display hex_digit_display_12 (.value(controlled_buffer_4_out[7:4]));  // open: dp
  Hex_Digit_Display hex_digit_display_13 (.value(controlled_buffer_5_out_4));  // open: dp
  Hex_Digit_Display hex_digit_display_14 (.value(controlled_buffer_4_out[3:0]));  // open: dp
  Hex_Digit_Display hex_digit_display_15 (.value(controlled_buffer_5_out_2));  // open: dp
  Hex_Digit_Display hex_digit_display_16 (.value(controlled_buffer_5_out_3));  // open: dp
  assign {controlled_buffer_5_out_4, controlled_buffer_5_out_3, controlled_buffer_5_out_2, controlled_buffer_5_out} = and_1_out ? Address : 16'bz;  // Controlled_Buffer controlled_buffer_5
  Hex_Digit_Display hex_digit_display_17 (.value(controlled_buffer_5_out));  // open: dp
  not not_3 (not_3_out, Tipo_R);
  and and_1 (and_1_out, not_3_out, not_4_out);
  not not_4 (not_4_out, Jump);

  // Notes on the sheet:
  //   Decoder
  //   Instruction
  //   rs
  //   rt
  //   Jump Address
  //   rd
  //   Address
endmodule

module decoder (
  input  [31:0] Address,
  output Tipo_R,
  output [15:0] Address_2,
  output [4:0] Rd,
  output [4:0] Rt,
  output [4:0] Rs,
  output [25:0] JAddress,
  output Add,
  output Sub,
  output And,
  output Or,
  output Mult,
  output Beq,
  output AddI,
  output Load,
  output Store,
  output Jump
);

  wire comparator_1_eq, comparator_2_eq, comparator_3_eq, comparator_5_eq, comparator_6_eq, comparator_7_eq,
       comparator_8_eq, comparator_9_eq, comparator_10_eq, comparator_11_eq, not_1_out, not_2_out, not_3_out,
       not_4_out, not_5_out;

  Comparator #(.width(6)) comparator_1 (.a(Address[5:0]), .b(6'b100000), .eq(comparator_1_eq));  // open: gt, lt
  not not_1 (not_1_out, Tipo_R);
  Comparator #(.width(6)) comparator_2 (.a(Address[31:26]), .b(6'b000100), .eq(comparator_2_eq));  // open: gt, lt
  not not_2 (not_2_out, Tipo_R);
  Comparator #(.width(6)) comparator_3 (.a(Address[31:26]), .b(6'b000010), .eq(comparator_3_eq));  // open: gt, lt
  and and_1 (Add, Tipo_R, comparator_1_eq);
  and and_2 (Beq, not_1_out, comparator_2_eq);
  and and_3 (Jump, not_2_out, comparator_3_eq);
  Comparator #(.width(6)) comparator_4 (.a(Address[31:26]), .b({6{1'b0}}), .eq(Tipo_R));  // open: gt, lt
  Comparator #(.width(6)) comparator_5 (.a(Address[5:0]), .b(6'b100010), .eq(comparator_5_eq));  // open: gt, lt
  Comparator #(.width(6)) comparator_6 (.a(Address[31:26]), .b(6'b001000), .eq(comparator_6_eq));  // open: gt, lt
  and and_4 (Sub, Tipo_R, comparator_5_eq);
  not not_3 (not_3_out, Tipo_R);
  and and_5 (AddI, not_3_out, comparator_6_eq);
  Comparator #(.width(6)) comparator_7 (.a(Address[5:0]), .b(6'b100100), .eq(comparator_7_eq));  // open: gt, lt
  and and_6 (And, Tipo_R, comparator_7_eq);
  not not_4 (not_4_out, Tipo_R);
  Comparator #(.width(6)) comparator_8 (.a(Address[31:26]), .b(6'b100011), .eq(comparator_8_eq));  // open: gt, lt
  and and_7 (Load, not_4_out, comparator_8_eq);
  Comparator #(.width(6)) comparator_9 (.a(Address[5:0]), .b(6'b100101), .eq(comparator_9_eq));  // open: gt, lt
  Comparator #(.width(6)) comparator_10 (.a(Address[31:26]), .b(6'b101011), .eq(comparator_10_eq));  // open: gt, lt
  and and_8 (Or, Tipo_R, comparator_9_eq);
  not not_5 (not_5_out, Tipo_R);
  and and_9 (Store, not_5_out, comparator_10_eq);
  Comparator #(.width(6)) comparator_11 (.a(Address[5:0]), .b(6'b011000), .eq(comparator_11_eq));  // open: gt, lt
  and and_10 (Mult, Tipo_R, comparator_11_eq);

  assign Address_2 = Address[15:0];
  assign JAddress = Address[25:0];
  assign Rd = Address[15:11];
  assign Rs = Address[25:21];
  assign Rt = Address[20:16];

  // Other names for the same wires on the sheet: Funct[5:0] = Address[5:0]; OpCode[5:0] = Address[31:26]
endmodule

module pc (
  input  clk,
  input  reset,
  output [31:0] data
);

  wire [31:0] adder_1_out, register_1_q;

  Register #(.width(32)) register_1 (.D(adder_1_out), .Q(register_1_q), .clk(clk), .clr(reset));  // open: en
  Adder #(.width(32)) adder_1 (.a(32'h1), .b(register_1_q), .out(adder_1_out));  // open: cin, cout
  ROM rom_1 (.pos(register_1_q[23:0]), .data(data));  // open: sel
endmodule

module RAM (
  input  [23:0] pos,
  input  [31:0] data,
  input  sel,
  input  clk,
  input  ld,
  input  clr
);

  RAM_part #(.addrWidth(24), .dataWidth(32)) ram_1 (.addr(pos), .data(data), .sel(sel), .clk(clk), .ld(ld), .clr(clr));
endmodule

module ROM (
  input  [23:0] pos,
  input  sel,
  output [31:0] data
);

  ROM_part #(.addrWidth(24), .dataWidth(32)) rom_1 (.addr(pos), .data(data), .sel(sel));

  // Notes on the sheet:
  //   contents of rom_1 (hex, n*v repeats v):
  //   12c6820 11a00001 1a90020 8c890001 1397020 8100008 120c820 329c824 13200001 810000c 20 1019fff7
  //   1495020
endmodule
